# Fritzing sketch laser relay complete Nov 2021 v0 - step 1 (saved by Fritzing 0.9.3b)
breadboards: 2

parts:
  Part1 = Arduino Uno (Rev3)
  Part2 = Arduino Uno (Rev3)
  LED3 = RGB LED (6 legs) [package="5 mm [THT]"]
  AM1 = AM2320 Humidity and Temperature Sensor [part_number="Adafruit #3721"]
  R3 = Resistor [tolerance=±5% resistance=10k package=THT]
  R4 = Resistor [tolerance=±5% resistance=10k package=THT]
  R5 = Resistor [tolerance=±5% resistance=560 package=THT]
  Q1 = LTR-301 [package=ltr-301]
  R11 = Resistor [tolerance=±5% resistance=330 package=THT]
  R12 = Resistor [tolerance=±5% resistance=1k package=THT]
  R13 = Resistor [tolerance=±5% resistance=10k package=THT]
  R14 = Resistor [tolerance=±5% resistance=10k package=THT]
  R15 = Resistor [tolerance=±5% resistance=10k package=THT]
  R16 = Resistor [tolerance=±5% resistance=10k package=THT]

nets:
  N1: Part1.D11_PWM/MOSI, R15.Pin_0
  N2: Part1.D13/SCK, R16.Pin_0
  N3: Part1.D2, R5.Pin_1, Q1.C
  N4: Part1.D5_PWM, R14.Pin_0
  N5: Part1.D6_PWM, R13.Pin_0
  N6: Part1.D7, R12.Pin_0
  N7: Part1.3V3, R11.Pin_0
  N8: Part1.5V, R5.Pin_0
  N9: Part1.GND, Q1.E
  N10: Part2.D13/SCK, LED3.Green
  N11: Part2.A4/SDA, AM1.SDA, R3.Pin_1
  N12: Part2.A5/SCL, AM1.SCL, R4.Pin_1
  5V: Part2.5V, AM1.VDD, R3.Pin_0, R4.Pin_0
  GND: Part2.GND, LED3.Blue1, AM1.GND

custom parts:
  AM2320 Humidity and Temperature Sensor: AM2320 I2C Humidity and Temperature Sensor
