# Fritzing sketch laser relay complete Nov 2021 v0 (saved by Fritzing 0.9.3b)
breadboards: 2

parts:
  Part1 = Arduino Uno (Rev3)
  Q1 = QRD1114 [package=qrd1114]
  R1 = Resistor [tolerance=±5% resistance=220 package=THT]
  Part2 = Arduino Uno (Rev3)
  R3 = Resistor [tolerance=±5% resistance=10k package=THT]
  LED3 = RGB LED (6 legs) [package="5 mm [THT]"]
  AM1 = AM2320 Humidity and Temperature Sensor [part_number="Adafruit #3721"]
  R4 = Resistor [tolerance=±5% resistance=10k package=THT]

nets:
  N1: Part1.D7, Q1.K, R1.Pin_1
  N2: Part1.GND, Q1.A, R1.Pin_0
  N3: Part2.D13/SCK, LED3.Green
  N4: Part2.A4/SDA, R3.Pin_1, AM1.SDA
  N5: Part2.A5/SCL, AM1.SCL, R4.Pin_1
  5V: Part2.5V, R3.Pin_0, AM1.VDD, R4.Pin_0
  GND: Part2.GND, LED3.Blue1, AM1.GND

custom parts:
  AM2320 Humidity and Temperature Sensor: AM2320 I2C Humidity and Temperature Sensor
